# Fritzing sketch stepperboard (saved by Fritzing 0.9.3b)
circuit board: 9.30697cm x 5.40257cm
breadboards: 1

parts:
  Pololu_A1 = Pololu A4988 [package=SO16]
  C1 = Capacitor Polarized [package=cpol-radial-100uf-25v]
  C2 = Capacitor Polarized [package=cpol-radial-100uf-25v]
  C3 = Capacitor Polarized [package=cpol-radial-100uf-25v]
  VCC2 = Battery
  Pololu_A3 = Pololu A4988 [package=SO16]
  Pololu_A2 = Pololu A4988 [package=SO16]
  J1 = female pin header, 2 pins [form="♀ (female)"]
  J2 = female pin header, 2 pins [form="♀ (female)"]
  J3 = female pin header, 2 pins [form="♀ (female)"]
  J12 = screw terminal, 2 pins
  J13 = screw terminal, 2 pins
  J14 = screw terminal, 2 pins
  J15 = screw terminal, 2 pins
  J16 = screw terminal, 2 pins
  J17 = screw terminal, 2 pins
  J18 = screw terminal, 2 pins

nets (from the pcb view):
  N1: Pololu_A1.RESET, Pololu_A1.SLEEP
  N2: Pololu_A1.STEP, J3.pin2
  N3: Pololu_A1.DIR, J3.pin1
  N4: Pololu_A1.GND#8, VCC2.-, Pololu_A3.GND#8, Pololu_A2.GND#8
  VDD: Pololu_A1.VDD, VCC2.+, Pololu_A3.VDD, Pololu_A2.VDD
  N5: Pololu_A1.1B, J12.pin2
  N6: Pololu_A1.1A, J12.pin1
  N7: Pololu_A1.2A, J13.pin2
  N8: Pololu_A1.2B, J13.pin1
  N9: Pololu_A1.GND#14, C1.-, C2.-, C3.-, Pololu_A3.GND#14, Pololu_A2.GND#14, J18.pin2
  N10: Pololu_A1.VMOT, C1.+, C2.+, C3.+, Pololu_A3.VMOT, Pololu_A2.VMOT, J18.pin1
  N11: Pololu_A3.RESET, Pololu_A3.SLEEP
  N12: Pololu_A3.STEP, J1.pin2
  N13: Pololu_A3.DIR, J1.pin1
  N14: Pololu_A3.1B, J17.pin2
  N15: Pololu_A3.1A, J17.pin1
  N16: Pololu_A3.2A, J16.pin2
  N17: Pololu_A3.2B, J16.pin1
  N18: Pololu_A2.RESET, Pololu_A2.SLEEP
  N19: Pololu_A2.STEP, J2.pin2
  N20: Pololu_A2.DIR, J2.pin1
  N21: Pololu_A2.1B, J15.pin2
  N22: Pololu_A2.1A, J15.pin1
  N23: Pololu_A2.2A, J14.pin2
  N24: Pololu_A2.2B, J14.pin1
