# Fritzing sketch Powerdist (saved by Fritzing 0.9.3b)
circuit board: 8.46667cm x 5.64444cm
breadboards: 1

parts:
  Drill = screw terminal, 2 pins
  Input = screw terminal, 2 pins
  Stepper = screw terminal, 2 pins
  Pump1 = screw terminal, 2 pins
  Pump2 = screw terminal, 2 pins

nets:
  N1: Drill.pin1, Input.pin1, Stepper.pin1, Pump1.pin1, Pump2.pin1
  N2: Drill.pin2, Input.pin2, Stepper.pin2, Pump1.pin2, Pump2.pin2
