# Fritzing sketch stepperboard (saved by Fritzing 0.9.3b)
circuit board: 8.46667cm x 5.64444cm
breadboards: 1

parts:
  Pololu_A1 = Pololu A4988 [package=SO16]
  Pololu_A2 = Pololu A4988 [package=SO16]
  Pololu_A3 = Pololu A4988 [package=SO16]
  C1 = Capacitor Polarized [package=cpol-radial-100uf-25v]
  C2 = Capacitor Polarized [package=cpol-radial-100uf-25v]
  C3 = Capacitor Polarized [package=cpol-radial-100uf-25v]
  M1 = Stepper Motor - Bipolar
  M3 = Stepper Motor - Bipolar
  M2 = Stepper Motor - Bipolar
  VCC1 = Battery
  Part1 = Arduino Mega ADK (Rev3)
  VCC2 = Battery

nets (from the breadboard view):
  N1: Pololu_A1.RESET, Pololu_A1.SLEEP
  N2: Pololu_A1.STEP, Part1.D2_PWM
  N3: Pololu_A1.DIR, Part1.D24
  N4: Pololu_A1.GND#8, Pololu_A2.GND#8, Pololu_A3.GND#8, Part1.GND, VCC2.-
  VDD: Pololu_A1.VDD, Pololu_A2.VDD, Pololu_A3.VDD, Part1.5V
  N5: Pololu_A1.1B, M3.D
  N6: Pololu_A1.1A, M3.B
  N7: Pololu_A1.2A, M3.C
  N8: Pololu_A1.2B, M3.A
  N9: Pololu_A1.GND#14, Pololu_A2.GND#14, Pololu_A3.GND#14, C1.+, C2.+, C3.+, VCC1.-
  N10: Pololu_A1.VMOT, Pololu_A2.VMOT, Pololu_A3.VMOT, C1.-, C2.-, C3.-, VCC1.+
  N11: Pololu_A2.RESET, Pololu_A2.SLEEP
  N12: Pololu_A2.STEP, Part1.D3_PWM
  N13: Pololu_A2.DIR, Part1.D23
  N14: Pololu_A2.1B, M1.D
  N15: Pololu_A2.1A, M1.B
  N16: Pololu_A2.2A, M1.C
  N17: Pololu_A2.2B, M1.A
  N18: Pololu_A3.RESET, Pololu_A3.SLEEP
  N19: Pololu_A3.STEP, Part1.D4_PWM
  N20: Pololu_A3.DIR, Part1.D22
  N21: Pololu_A3.1B, M2.D
  N22: Pololu_A3.1A, M2.B
  N23: Pololu_A3.2A, M2.C
  N24: Pololu_A3.2B, M2.A
  N25: Part1.VIN, VCC2.+
